# Fritzing sketch Schematic (saved by Fritzing 0.7.4b)

parts:
  Arduino1 = Arduino
  Parallax_PIR_Sensor1 = Parallax_PIR

nets:
  N1: Arduino1.D2, Parallax_PIR_Sensor1.OUT
  N2: Arduino1.+5V, Parallax_PIR_Sensor1.+
  N3: Arduino1.GND, Parallax_PIR_Sensor1.-

custom parts:
  : Motion detection sensor
